# Fritzing sketch flaesh_converter (saved by Fritzing 0.9.1b)
circuit board: 3.7cm x 2.1cm
stripboards: 1

parts:
  LD33V = Voltage Regulator - 3.3V [package="TO220 [THT]"]
  L4940V5 = Voltage Regulator - 5V [package="TO220 [THT]"]
  10uF = Electrolytic Capacitor [capacitance=10µF package="100 mil [THT, electrolytic]"]
  1000uF = Electrolytic Capacitor [capacitance=1mF package="200 mil [THT, electrolytic]"]
  0_1uf2 = Ceramic Capacitor [capacitance=100nF package="200 mil [THT, multilayer]"]
  0_1uf = Ceramic Capacitor [capacitance=100nF package="200 mil [THT, multilayer]"]
  IN = Screw terminal - 2 pins [package=THT]
  3_3V = Screw terminal - 2 pins [package=THT]
  5V = screw terminal, 2 pins
  22uF = Electrolytic Capacitor [capacitance=22µF package="100 mil [THT, electrolytic]"]

nets (from the schematic view):
  N1: LD33V.input_voltage, L4940V5.input_voltage, 1000uF.+, 0_1uf2.1, 0_1uf.1, IN.pin1
  GND: LD33V.GND, L4940V5.GND, 10uF.-, 1000uF.-, 0_1uf2.0, 0_1uf.0, IN.pin2, 3_3V.pin1, 5V.pin1, 22uF.-
  N2: LD33V.output_voltage, 10uF.+, 3_3V.pin2
  N3: L4940V5.output_voltage, 5V.pin2, 22uF.+

notes:
  +
  OUT
  GND
  IN
  -
